# Fritzing sketch Hardwareskizze (saved by Fritzing 0.9.10b)
breadboards: 1

parts:
  Mod1 = KY-004 Key Switch Module [package="Breakout board"]
  Part1 = Arduino Uno (Rev3)

nets:
  N1: Mod1.S, Part1.D2
  N2: Mod1.-, Part1.GND

custom parts:
  KY-004 Key Switch Module: Arduino Key Switch Module Keyes KY-004 is a push button that will output a high signal when pressed.
