# Fritzing sketch Hardwareskizze (saved by Fritzing 1.0.0d)
breadboards: 1

parts:
  Part1 = Arduino Uno (Rev3) - ICSP
  S1 = Pushbutton [package="[SMD]"]
  S2 = Pushbutton [package="[SMD]"]
  S3 = Pushbutton [package="[SMD]"]

nets:
  N1: Part1.D8, S1.Pin_1, S1.Pin_2
  N2: Part1.D9_PWM, S2.Pin_1, S2.Pin_2
  N3: Part1.D10_PWM/SS, S3.Pin_1, S3.Pin_2
  N4: Part1.GND, S1.Pin_3, S1.Pin_4, S2.Pin_3, S2.Pin_4, S3.Pin_3, S3.Pin_4
