# Fritzing sketch Atmega auf Breadboard (saved by Fritzing 0.9.10b)
breadboards: 1

parts:
  U1 = atmega328 [package=dip]
  XTAL1 = Crystal [frequency="16 Mhz" package=THT]
  R1 = Resistor [tolerance=±5% resistance=10k package="2010 [SMD]"]
  R2 = Resistor [tolerance=±5% resistance=220 package="2010 [SMD]"]
  R3 = Resistor [tolerance=±5% resistance=220 package="2010 [SMD]"]
  LED1 = smd LED [color="Red (633nm)" package="0805 [SMD]"]
  LED2 = smd LED [color="Red (633nm)" package="0805 [SMD]"]
  Mod1 = KY-023 Dual Axis Joystick Module [package="Breakout board"]

nets:
  N1: U1.RESET, R1.Pin_1
  VCC: U1.VCC, Mod1.+5V
  N2: U1.GND#7, R1.Pin_0, R2.Pin_1, R3.Pin_1, Mod1.GND
  N3: U1.XLAT1, XTAL1.pin_0
  N4: U1.XLAT2, XTAL1.pin_1
  N5: U1.D5_(PWM), LED1.cathode
  N6: U1.D6_(PWM), LED2.cathode
  N7: U1.D7, Mod1.SW
  N8: U1.A0, Mod1.VRy
  N9: U1.A1, Mod1.VRx
  N10: R2.Pin_0, LED1.anode
  N11: R3.Pin_0, LED2.anode

custom parts:
  KY-023 Dual Axis Joystick Module: KY-023 Dual-Axis Joystick Module.
