# Fritzing sketch Buttons - Hardwareskizze (saved by Fritzing 1.0.0d)
breadboards: 1

parts:
  Part1 = Arduino Uno (Rev3) - ICSP
  S1 = Pushbutton [package="[THT]"]
  R2 = Resistor [tolerance=±5% resistance=50000 package="2010 [SMD]"]
  R3 = Resistor [tolerance=±5% resistance=50000 package="2010 [SMD]"]
  S2 = Pushbutton [package="[THT]"]
  S3 = Pushbutton [package="[THT]"]
  R5 = Resistor [tolerance=±5% power=0.25W resistance=1000 package=THT]

nets:
  N1: Part1.GND, S2.Pin_3, S2.Pin_4
  N2: S1.Pin_2, R2.Pin_1, R3.Pin_0
  N3: S1.Pin_3, S1.Pin_4, R2.Pin_0
  N4: R3.Pin_1, S3.Pin_1
  N5: S2.Pin_1, S2.Pin_2, R5.Pin_0
