# Fritzing sketch Hardwareskizze (saved by Fritzing 1.0.0d)
breadboards: 1

parts:
  Part1 = Arduino Uno (Rev3) - ICSP
  R1 = Rotary Potentiometer (Small) [maximum_resistance=10kΩ knob_status=50% power=0.5W package=THT]
  R2 = Resistor [tolerance=±5% power=0.25W resistance=220 package=THT]
  LED1 = smd LED [color="Red (633nm)" package="1206 [SMD]"]
  R3 = Resistor [tolerance=±5% power=0.25W resistance=220 package=THT]
  LED2 = smd LED [color="Red (633nm)" package="1206 [SMD]"]
  R4 = Resistor [tolerance=±5% power=0.25W resistance=220 package=THT]
  LED3 = smd LED [color="Red (633nm)" package="1206 [SMD]"]
  R5 = Resistor [tolerance=±5% power=0.25W resistance=220 package=THT]
  LED4 = smd LED [color="Red (633nm)" package="1206 [SMD]"]

nets:
  N1: Part1.A0, R1.wiper
  N2: Part1.ICSP_MISO, Part1.D12/MISO, LED2.anode
  N3: Part1.D10_PWM/SS, LED4.anode
  N4: Part1.D11_PWM/MOSI, LED3.anode
  N5: Part1.D13/SCK, LED1.anode
  N6: Part1.5V, R1.leg1
  N7: Part1.GND, R1.leg2, R2.Pin_0, R3.Pin_0, R4.Pin_0, R5.Pin_0
  N8: R2.Pin_1, LED1.cathode
  N9: R3.Pin_1, LED2.cathode
  N10: R4.Pin_1, LED3.cathode
  N11: R5.Pin_1, LED4.cathode
