# Fritzing sketch Hardwareskizze (saved by Fritzing 1.0.0d)
breadboards: 1

parts:
  Part1 = Arduino Uno (Rev3) - ICSP
  LCD1 = LCD screen
  R3 = 6mm Trimmer Potentiometer [maximum_resistance=10kΩ knob_status=50% power=0.5W package=THT]
  S1 = Pushbutton [package="[THT]"]
  S2 = Pushbutton [package="[THT]"]

nets:
  N1: Part1.ICSP_MOSI, Part1.D11_PWM/MOSI, LCD1.DB7
  GND: Part1.GND, LCD1.VSS, LCD1.R/W, LCD1.LED-, R3.leg1, S1.Pin_1, S1.Pin_2, S2.Pin_1, S2.Pin_2
  N2: Part1.D8, LCD1.DB4
  N3: Part1.D9_PWM, LCD1.DB5
  N4: Part1.D10_PWM/SS, LCD1.DB6
  N5: Part1.D12/MISO, S2.Pin_3, S2.Pin_4
  N6: Part1.D13/SCK, S1.Pin_3, S1.Pin_4
  N7: Part1.D2, LCD1.RS
  N8: Part1.D3_PWM, LCD1.E
  N9: Part1.D4, LCD1.DB0
  N10: Part1.D5_PWM, LCD1.DB1
  N11: Part1.D6_PWM, LCD1.DB2
  N12: Part1.D7, LCD1.DB3
  5V: Part1.5V, LCD1.VDD, LCD1.LED+, R3.leg2
  N13: LCD1.V0, R3.wiper
