# Fritzing sketch Hardwareskizze (saved by Fritzing 1.0.0d)

parts:
  Part1 = Arduino Uno (Rev3) - ICSP
  Part2 = Arduino Uno (Rev3) - ICSP
  Part3 = Arduino Uno (Rev3) - ICSP

nets:
  GND: Part1.GND, Part2.GND, Part3.GND
  N1: Part1.D2, Part2.D5_PWM
  N2: Part1.D3_PWM, Part2.D4
  N3: Part2.D2, Part3.D5_PWM
  N4: Part2.D3_PWM, Part3.D4
