# Fritzing sketch Hardwareskizze (saved by Fritzing 0.9.10b)
breadboards: 1

parts:
  SEN1 = US-100 Ultrasonic Distance Sensor
  Mod1 = KY-004 Key Switch Module [package="Breakout board"]
  Mod2 = KY-012 Active Buzzer Module [package="Breakout board"]
  Part1 = Arduino Uno (Rev3)

nets:
  VCC: SEN1.VCC, Part1.5V
  N1: SEN1.TRIG, Part1.D3_PWM
  N2: SEN1.ECHO, Part1.D4
  GND: SEN1.GND, SEN1.GND-2, Mod1.-, Mod2.-, Part1.GND
  N3: Mod1.S, Part1.D2
  N4: Mod2.S, Part1.D5_PWM

custom parts:
  KY-004 Key Switch Module: Arduino Key Switch Module Keyes KY-004 is a push button that will output a high signal when pressed.
  KY-012 Active Buzzer Module: Active Piezoelectric Buzzer Module KY-012, it produces single-tone sound when signal is high. (Special thanks to vanepp for fixing the PCB holes and other errors)
