# Fritzing sketch LED-Matrix (saved by Fritzing 0.9.10b)
breadboards: 1

parts:
  Part1 = Arduino Uno (Rev3) - ICSP
  LED25 = LED - 3mm [color="Red (633nm)" current=0.030 package="3 mm [THT]"]
  R5 = Resistor [tolerance=±5% resistance=680 package="0805 [SMD]"]
  LED26 = LED - 3mm [color="Red (633nm)" current=0.030 package="3 mm [THT]"]
  LED27 = LED - 3mm [color="Red (633nm)" current=0.030 package="3 mm [THT]"]
  LED28 = LED - 3mm [color="Red (633nm)" current=0.030 package="3 mm [THT]"]
  LED29 = LED - 3mm [color="Red (633nm)" current=0.030 package="3 mm [THT]"]
  LED30 = LED - 3mm [color="Red (633nm)" current=0.030 package="3 mm [THT]"]
  LED31 = LED - 3mm [color="Red (633nm)" current=0.030 package="3 mm [THT]"]
  LED32 = LED - 3mm [color="Red (633nm)" current=0.030 package="3 mm [THT]"]
  R6 = Resistor [tolerance=±5% resistance=680 package="0805 [SMD]"]
  Mod1 = KY-029 Dual Color LED Module [package="Breakout board"]
  S1 = Pushbutton [package="[THT]"]

nets:
  N1: Part1.A0, Mod1.-
  N2: Part1.D8, S1.Pin_1, S1.Pin_2
  N3: Part1.D2, R5.Pin_0
  N4: Part1.D3_PWM, R6.Pin_0
  N5: Part1.D4, LED28.cathode, LED29.cathode
  N6: Part1.D5_PWM, LED27.cathode, LED32.cathode
  N7: Part1.D6_PWM, LED26.cathode, LED30.cathode
  N8: Part1.D7, LED25.cathode, LED31.cathode
  N9: Part1.5V, Mod1.R
  N10: Part1.GND, Mod1.G, S1.Pin_3, S1.Pin_4
  N11: LED25.anode, R5.Pin_1, LED26.anode, LED27.anode, LED28.anode
  N12: LED29.anode, LED30.anode, LED31.anode, LED32.anode, R6.Pin_1

notes:
  KY-018 Photoresistor

custom parts:
  KY-029 Dual Color LED Module: KY-029 Dual Color LED Module consist of a common cathode 5mm red/green LED.
