# Fritzing sketch Atmega auf Breadboard (minimal) (saved by Fritzing 0.9.10b)
breadboards: 1

parts:
  Y2 = CRYSTAL [package=crystal-smd-10.5x4.8-2pin]
  U1 = atmega328 [package=dip]
  Part1 = Arduino Uno (Rev3) - ICSP

nets:
  N1: Y2.1, U1.XLAT1
  N2: Y2.2, U1.XLAT2
  VCC: U1.VCC, Part1.5V
  GND: U1.GND, Part1.GND

notes:
  Oder andere 5V Stromquelle
