# Fritzing sketch Atmega auf Breadboard (vollständig) (saved by Fritzing 0.9.10b)
breadboards: 1

parts:
  IC1 = Voltage Regulator [package=to220-adj]
  Y2 = CRYSTAL [package=crystal-smd-10.5x4.8-2pin]
  C3 = Capacitor Polarized [package=cpol-radial-1000uf-25v]
  U1 = atmega328 [package=dip]
  R2 = Resistor [tolerance=±5% resistance=10k package="1206 [SMD]"]
  C2 = Capacitor [package=cap-pth-small2]
  VCC1 = Battery block 9V
  C1 = Capacitor [package=cap-pth-small2]
  C4 = Capacitor Polarized [package=cpol-radial-1000uf-25v]

nets:
  N1: IC1.ADJ, VCC1.+, C4.+
  GND: IC1.IN, C3.-, U1.GND, R2.Pin_0, C2.2, VCC1.-, C1.2, C4.-
  N2: IC1.OUT, C3.+, U1.VCC
  N3: Y2.1, U1.XLAT1, C2.1
  N4: Y2.2, U1.XLAT2, C1.1
  N5: U1.RESET, R2.Pin_1

notes:
  22µF Kondensatoren empfohlen, aber für Batteriebetrieb nicht notwendig.
  22pF Kondensatoren für Kristal empfohlen, aber zum Experimentieren nicht zwingend notwendig.
  10k Widerstand empfohlen zum Experimentieren aber nicht zwingend notwendig.
