# Fritzing sketch Hardwareskizze (saved by Fritzing 0.9.10b)
breadboards: 1

parts:
  J1 = T Cobbler Plus
  Mod1 = KY-004 Key Switch Module [package="Breakout board"]
  Mod2 = KY-029 Dual Color LED Module [package="Breakout board"]

nets:
  N1: J1.SDA, Mod1.S
  N2: J1.#17, Mod2.G
  N3: Mod1.-, Mod2.-

custom parts:
  T Cobbler Plus: The T-Cobbler Plus is an add on prototyping board from Adafruit specifically designed for the Raspberry Pi B+ that can break out all those tasty power, GPIO, I2C and SPI pins from the 40-pin header onto a solderless breadboard. This set will make "cobbling together" prototypes with the Pi super easy. The T-Cobbler Plus can plug into any solderless breadboard.
  KY-004 Key Switch Module: Arduino Key Switch Module Keyes KY-004 is a push button that will output a high signal when pressed.
  KY-029 Dual Color LED Module: KY-029 Dual Color LED Module consist of a common cathode 5mm red/green LED.
