# Fritzing sketch Hardwareskizze (saved by Fritzing 0.9.10b)
breadboards: 1

parts:
  SEN1 = US-100 Ultrasonic Distance Sensor
  Mod1 = KY-004 Key Switch Module [package="Breakout board"]
  Mod2 = KY-012 Active Buzzer Module [package="Breakout board"]
  J1 = T Cobbler Plus
  Part1 = Adafruit 4-channel I2C-safe Bi-directional Logic Level Converter [part_number="Adafruit #757"]

nets:
  N1: SEN1.VCC, J1.5.0V#1, Part1.HV
  N2: SEN1.TRIG, Part1.B1
  N3: SEN1.ECHO, Part1.B2
  GND: SEN1.GND, SEN1.GND-2, Mod1.-, Mod2.-, J1.GND#8, J1.#21, Part1.GND
  N4: Mod1.S, J1.#26
  N5: J1.3V3, Part1.LV
  N6: J1.#27, Part1.A1
  N7: J1.#22, Part1.A2

custom parts:
  KY-004 Key Switch Module: Arduino Key Switch Module Keyes KY-004 is a push button that will output a high signal when pressed.
  KY-012 Active Buzzer Module: Active Piezoelectric Buzzer Module KY-012, it produces single-tone sound when signal is high. (Special thanks to vanepp for fixing the PCB holes and other errors)
  T Cobbler Plus: The T-Cobbler Plus is an add on prototyping board from Adafruit specifically designed for the Raspberry Pi B+ that can break out all those tasty power, GPIO, I2C and SPI pins from the 40-pin header onto a solderless breadboard. This set will make "cobbling together" prototypes with the Pi super easy. The T-Cobbler Plus can plug into any solderless breadboard.
  Adafruit 4-channel I2C-safe Bi-directional Logic Level Converter: Because the Arduino (and Basic Stamp) are 5V devices, and most modern sensors, displays, flash cards and modes are 3.3V-only, many makers find that they need to perform level shifting/conversion to protect the 3.3V device from 5V. We do have some other handy level shifters in the shop, from the DIP 74LVC245 to the fancy bi-directional TXB0108. However, neither of these are happy to work with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
